# Fritzing sketch Sousduino (saved by Fritzing 0.9.2b)
circuit board: 5cm x 4.1cm
breadboards: 1

parts:
  R1 = Resistor [tolerance=±5% resistance=33k package=THT]
  R2 = Resistor [tolerance=±5% resistance=470 package=THT]
  R4 = Resistor [tolerance=±5% resistance=1k package=THT]
  R5 = Resistor [tolerance=±5% resistance=33k package=THT]
  U5 = MOC3031-M [part_number=MOC3021 package=dil06]
  J2 = screw terminal, 2 pins
  J3 = male pin header, 4 pins [form="♂ (male)"]
  U7 = Optocoupler [package=THT]
  R3 = Resistor [tolerance=±5% resistance=10k package=THT]
  Onderdeel1 = DB107 [package=THT]
  J4 = screw terminal, 2 pins
  TRI1 = BTA Triac [package="TO220 [THT]"]

nets:
  N1: R1.Pin_0, Onderdeel1.Pin_2
  N2: R1.Pin_1, R4.Pin_1, J2.pin1, TRI1.A2
  N3: R2.Pin_0, J3.pin4
  N4: R2.Pin_1, U5.1
  N5: R4.Pin_0, U5.6
  N6: R5.Pin_0, Onderdeel1.Pin_1
  N7: R5.Pin_1, J2.pin2, J4.pin1
  N8: U5.2, J3.pin3, U7.Pin_5
  N9: U5.4, TRI1.G
  N10: J3.pin1, R3.Pin_0
  N11: J3.pin2, U7.Pin_4, R3.Pin_1
  N12: U7.Pin_1, Onderdeel1.Pin_3
  N13: U7.Pin_2, Onderdeel1.Pin_4
  N14: J4.pin2, TRI1.A1

notes:
  load
  Mains
  VCC
  ZERO
  GND
  SW
  -
  +
  MOC3021
  BTA41
  Bridge
  4N25
  By Dries Willemsens

custom parts:
  DB107: Bridge rectifier
  BTA Triac: BTA16
